// Logisim project Basic-gate.circ as structural Verilog: 1 circuit, main circuit main
module main (
  input  in_1,
  input  in_2,
  input  in_3
);

  wire not_1_out, not_2_out, not_3_out, or_1_out, or_2_out, or_3_out, or_4_out, or_5_out, or_6_out, or_7_out,
       X_prime_Y_prime_out, X_prime_Z_out, X_prime_Z_prime_out, XY_prime_out, XZ_prime_out, Y_prime_Z_out,
       Y_prime_Z_prime_out, YZ_out;

  not not_1 (not_1_out, in_1);
  not not_2 (not_2_out, in_2);
  not not_3 (not_3_out, in_3);
  and Y_prime_Z_prime (Y_prime_Z_prime_out, not_2_out, not_3_out);
  and YZ (YZ_out, in_2, in_3);
  and XY_prime (XY_prime_out, in_1, not_2_out);
  and Y_prime_Z (Y_prime_Z_out, not_2_out, in_3);
  and X_prime_Z_prime (X_prime_Z_prime_out, not_1_out, not_3_out);
  and X_prime_Y_prime (X_prime_Y_prime_out, not_1_out, not_2_out);
  and XZ_prime (XZ_prime_out, in_1, not_3_out);
  and X_prime_Z (X_prime_Z_out, not_1_out, in_3);
  or or_1 (or_1_out, not_1_out, Y_prime_Z_prime_out, YZ_out);
  or or_2 (or_2_out, YZ_out, XY_prime_out);
  or or_3 (or_3_out, Y_prime_Z_out, XY_prime_out);
  or or_4 (or_4_out, not_1_out, Y_prime_Z_prime_out, YZ_out);
  or or_5 (or_5_out, X_prime_Z_prime_out, YZ_out);
  or or_6 (or_6_out, X_prime_Z_prime_out, X_prime_Y_prime_out);
  or or_7 (or_7_out, in_2, XZ_prime_out, X_prime_Z_out);
  _7_Segment_Display u_7_segment_display_1 (
    .g(or_7_out), .f(or_6_out), .a(or_1_out), .b(or_2_out), .e(or_5_out), .d(or_4_out), .c(or_3_out));  // open: dp
endmodule
