// Logisim project MUX4X1.circ as structural Verilog: 1 circuit, main circuit main
module main (
  input  _0,
  input  _1,
  input  Z,
  input  [1:0] in_4
);

  wire multiplexer_1_out, multiplexer_2_out, multiplexer_3_out, multiplexer_4_out, multiplexer_5_out,
       multiplexer_6_out, multiplexer_7_out, not_1_out;

  not not_1 (not_1_out, Z);
  Multiplexer #(.select(2), .enable("false")) multiplexer_1 (
    .in0(_1), .in1(_1), .in2(not_1_out), .in3(Z), .out(multiplexer_1_out), .sel(in_4));
  Multiplexer #(.select(2), .enable("false")) multiplexer_2 (
    .in0(_0), .in1(Z), .in2(_1), .in3(Z), .out(multiplexer_2_out), .sel(in_4));
  Multiplexer #(.select(2), .enable("false")) multiplexer_3 (
    .in0(Z), .in1(_0), .in2(_1), .in3(_0), .out(multiplexer_3_out), .sel(in_4));
  _7_Segment_Display u_7_segment_display_1 (
    .g(multiplexer_7_out), .f(multiplexer_6_out), .a(multiplexer_1_out), .b(multiplexer_2_out),
    .e(multiplexer_5_out), .d(multiplexer_4_out), .c(multiplexer_3_out));  // open: dp
  Multiplexer #(.select(2), .enable("false")) multiplexer_4 (
    .in0(_1), .in1(_1), .in2(not_1_out), .in3(Z), .out(multiplexer_4_out), .sel(in_4));
  Multiplexer #(.select(2), .enable("false")) multiplexer_5 (
    .in0(not_1_out), .in1(_1), .in2(_0), .in3(Z), .out(multiplexer_5_out), .sel(in_4));
  Multiplexer #(.select(2), .enable("false")) multiplexer_6 (
    .in0(_1), .in1(not_1_out), .in2(_0), .in3(_0), .out(multiplexer_6_out), .sel(in_4));
  Multiplexer #(.select(2), .enable("false")) multiplexer_7 (
    .in0(Z), .in1(_1), .in2(not_1_out), .in3(_1), .out(multiplexer_7_out), .sel(in_4));
endmodule
